# Fritzing sketch Untitled Sketch (saved by Fritzing 1.0.4)
breadboards: 1

parts:
  A1 = Particle - Photon2
  OLED_I2C1 = OLED 128x64 I2C Monochrome Display
  M1 = BMP280
  Part1 = MQ-131 breakout
  Relay1 = Relay - 6 pins [package="DIP (Dual Inline) [THT]"]
  SENS1 = SoilWatch 10
  Q1 = PNP-Transistor [package="TO92 [THT]"]
  R1 = Resistor [tolerance=±5% power=0.25W resistance=220 package=THT]
  R2 = Resistor [tolerance=±5% power=0.25W resistance=2200 package=THT]
  WATER_PUMP1 = water pump/motor  # not connected

nets:
  VCC: A1.Pin_2, A1.Pin_31, OLED_I2C1.VDD, M1.VIN, Part1.VCC, Relay1.VCC, SENS1.VCC
  GND: A1.Pin_4, A1.Pin_30, A1.Pin_35, OLED_I2C1.GND, M1.GND, Part1.GND, Relay1.GND, SENS1.GND
  N1: A1.Pin_6, SENS1.OUT
  N2: A1.Pin_8, Part1.AO
  N3: A1.Pin_14, Q1.B, R1.Pin_1
  N4: A1.Pin_17, OLED_I2C1.SDA, M1.SDA
  N5: A1.Pin_18, OLED_I2C1.SCK, M1.SCL
  N6: A1.Pin_26, Q1.C, R1.Pin_0, R2.Pin_0
  N7: Relay1.IN, Q1.E, R2.Pin_1

custom parts:
  Particle - Photon2: The Photon 2 is a microcontroller and Wi-Fi networking developed by particle. Features: 802.11a/b/g/n Wi-Fi, 2.4 GHz and 5 GHz Integrated PCB antenna Integrated U.FL connector for external antenna Integrated RF switch BLE 5 using same antenna as Wi-Fi Realtek RTL8721DM MCU ARM Cortex M33 CPU, 200 MHz 2048 KB (2 MB) user application maximum size 3072 KB (3 MB) of RAM available to user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
  BMP280: Temperature Humidity Barometric presure Sensor, I2C
  MQ-131 breakout: SKU: 101282
  Relay - 6 pins: A DIP stand-in part for whatever IC you want. With 6 pins on a 900mil dual inline package (DIP) footprint.
  SoilWatch 10: SoilWatch 10 - Capacitive soil moisture sensor
  water pump/motor: WATER PUMP BY ARDUBLOCKTR
